// Logisim project Adder1.circ as structural Verilog: 1 circuit, main circuit main
module main (
  input  A,
  input  B,
  input  Ci,
  output C0,
  output S0
);

  wire and_1_out, and_2_out, xor_1_out;

  xor xor_1 (xor_1_out, A, B);
  and and_1 (and_1_out, A, B);
  and and_2 (and_2_out, xor_1_out, Ci);
  xor xor_2 (C0, and_1_out, and_2_out);
  xor xor_3 (S0, xor_1_out, Ci);
endmodule
