// Logisim project Adder16.circ as structural Verilog: 1 circuit, main circuit main
module main (
  input  [15:0] A,
  input  [15:0] B,
  input  Co,
  output Co_2,
  output [15:0] S
);

  wire main_1_co, main_2_co, main_3_co;

  Adder4_main main_1 (.A(A[3:0]), .B(B[3:0]), .Ci(Co), .Co(main_1_co), .So(S[3:0]));
  Adder4_main main_2 (.A(A[7:4]), .B(B[7:4]), .Ci(main_1_co), .Co(main_2_co), .So(S[7:4]));
  Adder4_main main_3 (.A(A[11:8]), .B(B[11:8]), .Ci(main_2_co), .Co(main_3_co), .So(S[11:8]));
  Adder4_main main_4 (.A(A[15:12]), .B(B[15:12]), .Ci(main_3_co), .Co(Co_2), .So(S[15:12]));
endmodule
