// Logisim project Adder32.circ as structural Verilog: 1 circuit, main circuit main
module main (
  input  [31:0] A,
  input  [31:0] B,
  input  Ci,
  output Co,
  output [31:0] So
);

  wire main_1_co_2;

  Adder16_main main_1 (.A(A[15:0]), .B(B[15:0]), .Co(Ci), .Co_2(main_1_co_2), .S(So[15:0]));
  Adder16_main main_2 (.A(A[31:16]), .B(B[31:16]), .Co(main_1_co_2), .Co_2(Co), .S(So[31:16]));
endmodule
