// Logisim project Adder4.circ as structural Verilog: 1 circuit, main circuit main
module main (
  input  [3:0] A,
  input  [3:0] B,
  input  Ci,
  output Co,
  output [3:0] So
);

  wire main_2_c0, main_3_c0, main_4_c0;

  Adder1_main main_1 (.A(A[3]), .B(B[3]), .Ci(main_2_c0), .C0(Co), .S0(So[3]));
  Adder1_main main_2 (.A(A[2]), .B(B[2]), .Ci(main_3_c0), .C0(main_2_c0), .S0(So[2]));
  Adder1_main main_3 (.A(A[1]), .B(B[1]), .Ci(main_4_c0), .C0(main_3_c0), .S0(So[1]));
  Adder1_main main_4 (.A(A[0]), .B(B[0]), .Ci(Ci), .C0(main_4_c0), .S0(So[0]));
endmodule
