// Logisim project Controller.circ as structural Verilog: 1 circuit, main circuit main
module main (
  input  Op5,
  input  Op4,
  input  Op3,
  input  Op2,
  input  Op1,
  input  Op0,
  input  Fc5,
  input  fc4,
  input  fc3,
  input  fc2,
  input  fc1,
  input  fc0
);

  wire add_out, beq_out, fcAdd_out, fcSub_out, FuncAdd_out, FuncSub_out, lw_out, not_1_out, not_2_out,
       not_3_out, not_4_out, not_5_out, not_7_out, not_8_out, not_9_out, not_10_out, not_11_out, not_12_out,
       not_13_out, not_14_out, not_15_out, not_16_out, not_18_out, not_19_out, not_20_out, not_21_out,
       not_22_out, not_23_out, not_24_out, not_25_out, not_26_out, ori_out, sub_out, sw_out;
  wire [5:0] undriven;

  not not_1 (not_1_out, Op5);
  not not_2 (not_2_out, Op4);
  not not_3 (not_3_out, Op3);
  not not_4 (not_4_out, Op2);
  not not_5 (not_5_out, Op1);
  // NOT_Gate not_6 has open pins: in=Fc5, out=open
  not not_7 (not_7_out, Op0);
  not not_8 (not_8_out, fc4);
  not not_9 (not_9_out, fc3);
  and add (add_out, not_1_out, not_2_out, not_3_out, fcAdd_out, not_4_out, not_5_out, not_7_out);
  and sub (sub_out, not_1_out, not_2_out, not_3_out, fcSub_out, not_4_out, not_5_out, not_7_out);
  and ori (ori_out, not_1_out, not_2_out, Op3, Op2, not_5_out, Op0);
  and lw (lw_out, Op5, not_2_out, not_3_out, not_4_out, Op1, Op0);
  and sw (sw_out, Op5, not_2_out, Op3, not_4_out, Op1, Op0);
  and beq (beq_out, not_1_out, not_2_out, not_3_out, Op2, not_5_out, not_7_out);
  // OR_Gate RegDst has open pins: in0=add_out, in1=sub_out, out=open
  not not_10 (not_10_out, fc1);
  not not_11 (not_11_out, fc2);
  // OR_Gate ALUSrc has open pins: in0=ori_out, in1=lw_out, in2=sw_out, out=open
  not not_12 (not_12_out, fc0);
  // OR_Gate MemtoReg has open pins: in1=lw_out, out=open
  and fcAdd (fcAdd_out, Fc5, not_8_out, not_9_out, not_11_out, not_10_out, not_12_out);
  and fcSub (fcSub_out, Fc5, not_8_out, not_9_out, not_11_out, fc1, not_12_out);
  // OR_Gate RegWrite has open pins: in0=add_out, in1=sub_out, in2=ori_out, in3=lw_out, out=open
  // OR_Gate MemWrite has open pins: in1=sw_out, out=open
  // OR_Gate nPC_Sel has open pins: in1=beq_out, out=open
  // OR_Gate ExtOp has open pins: in0=lw_out, in1=sw_out, out=open
  not not_13 (not_13_out, undriven[0]);
  not not_14 (not_14_out, undriven[1]);
  not not_15 (not_15_out, undriven[2]);
  not not_16 (not_16_out, undriven[5]);
  not not_17 (undriven[3], undriven[3]);
  not not_18 (not_18_out, not_13_out);
  not not_19 (not_19_out, not_14_out);
  not not_20 (not_20_out, not_15_out);
  not not_21 (not_21_out, undriven[3]);
  not not_22 (not_22_out, not_16_out);
  not not_23 (not_23_out, not_13_out);
  not not_24 (not_24_out, not_15_out);
  not not_25 (not_25_out, not_15_out);
  not not_26 (not_26_out, undriven[3]);
  and FuncAdd (FuncAdd_out, undriven[0], not_18_out, not_19_out, not_20_out, not_21_out, not_22_out);
  and FuncSub (FuncSub_out, undriven[0], not_23_out, not_24_out, not_25_out, undriven[3], not_26_out);
endmodule
