// Logisim project Subber1.circ as structural Verilog
module Subber1 (
  input  A,
  input  B,
  input  Ci,
  output Co,
  output D
);

  wire and_1_out, and_2_out, and_3_out, and_4_out, and_5_out, and_6_out, and_7_out, not_1_out, not_2_out,
       not_3_out, not_4_out, not_5_out, not_6_out, not_7_out, not_8_out;

  not not_1 (not_1_out, A);
  not not_2 (not_2_out, A);
  not not_3 (not_3_out, A);
  not not_4 (not_4_out, B);
  not not_5 (not_5_out, A);
  not not_6 (not_6_out, Ci);
  not not_7 (not_7_out, B);
  not not_8 (not_8_out, Ci);
  and and_1 (and_1_out, not_1_out, Ci);
  and and_2 (and_2_out, not_2_out, B);
  and and_3 (and_3_out, B, Ci);
  and and_4 (and_4_out, not_3_out, not_4_out, Ci);
  and and_5 (and_5_out, not_5_out, B, not_6_out);
  and and_6 (and_6_out, A, not_7_out, not_8_out);
  and and_7 (and_7_out, A, B, Ci);
  or or_1 (Co, and_1_out, and_2_out, and_3_out);
  or or_2 (D, and_4_out, and_5_out, and_6_out, and_7_out);
endmodule

module Subber4 (
  input  Ci,
  input  [3:0] A,
  input  [3:0] B,
  output [3:0] D,
  output Co
);

  wire subber1_1_co, subber1_2_co, subber1_3_co;

  Subber1 subber1_1 (.A(A[0]), .B(B[0]), .Ci(Ci), .Co(subber1_1_co), .D(D[0]));
  Subber1 subber1_2 (.A(A[1]), .B(B[1]), .Ci(subber1_1_co), .Co(subber1_2_co), .D(D[1]));
  Subber1 subber1_3 (.A(A[2]), .B(B[2]), .Ci(subber1_2_co), .Co(subber1_3_co), .D(D[2]));
  Subber1 subber1_4 (.A(A[3]), .B(B[3]), .Ci(subber1_3_co), .Co(Co), .D(D[3]));
endmodule

module Subber16 (
  input  Ci,
  input  [15:0] A,
  input  [15:0] B,
  output [15:0] D,
  output Co
);

  wire subber4_1_co, subber4_2_co, subber4_3_co;

  Subber4 subber4_1 (.Ci(Ci), .A(A[3:0]), .B(B[3:0]), .D(D[3:0]), .Co(subber4_1_co));
  Subber4 subber4_2 (.Ci(subber4_1_co), .A(A[7:4]), .B(B[7:4]), .D(D[7:4]), .Co(subber4_2_co));
  Subber4 subber4_3 (.Ci(subber4_2_co), .A(A[11:8]), .B(B[11:8]), .D(D[11:8]), .Co(subber4_3_co));
  Subber4 subber4_4 (.Ci(subber4_3_co), .A(A[15:12]), .B(B[15:12]), .D(D[15:12]), .Co(Co));
endmodule

module Subber32 (
  input  Ci,
  input  [31:0] A,
  input  [31:0] B,
  output [31:0] D,
  output Co
);

  wire subber16_1_co;

  Subber16 subber16_1 (.Ci(Ci), .A(A[15:0]), .B(B[15:0]), .D(D[15:0]), .Co(subber16_1_co));
  Subber16 subber16_2 (.Ci(subber16_1_co), .A(A[31:16]), .B(B[31:16]), .D(D[31:16]), .Co(Co));
endmodule
