// Logisim project mips-lite-noprobe.circ as structural Verilog: 12 circuits, main circuit main
module main (
  input  Reset
);

  wire alu1_1_zero, Clk_out, controller3_1_alusrc, controller3_1_extop, controller3_1_memtoreg,
       controller3_1_memwrite, controller3_1_npc_sel, controller3_1_regdst, controller3_1_regwrite;
  wire [3:0] controller3_1_aluctrl;
  wire [4:0] multiplexer_1_out;
  wire [15:0] ifu_1_instr;
  wire [31:0] alu1_1_result, dm_1_wdata, ext_1_out_3, gpr1_1_rdata1, gpr1_1_rdata2, multiplexer_2_out;
  wire [31:16] ifu_1_instr_2;

  Clock Clk (.out(Clk_out));
  IFU ifu_1 (
    .IfBeq(controller3_1_npc_sel), .Zero(alu1_1_zero), .Clk(Clk_out), .Reset(Reset),
    .Instr({ifu_1_instr_2, ifu_1_instr}));
  Multiplexer #(.width(5)) multiplexer_1 (
    .in0(ifu_1_instr_2[20:16]), .in1(ifu_1_instr[15:11]), .out(multiplexer_1_out),
    .sel(controller3_1_regdst), .en(1'b1));
  EXT ext_1 (._16Bits(ifu_1_instr), .ExtOP(controller3_1_extop), .out_3(ext_1_out_3));
  GPR1 gpr1_1 (
    .RS1(ifu_1_instr_2[25:21]), .RS2(ifu_1_instr_2[20:16]), .RegWrite(controller3_1_regwrite),
    .RD_WA(multiplexer_1_out), .WData(dm_1_wdata), .ResetReg(Reset), .Clk(Clk_out), .RData1(gpr1_1_rdata1),
    .RData2(gpr1_1_rdata2));
  Controller3 controller3_1 (
    .Op(ifu_1_instr_2[31:26]), .Func(ifu_1_instr[5:0]), .RegDst(controller3_1_regdst),
    .ALUSrc(controller3_1_alusrc), .MemtoReg(controller3_1_memtoreg), .RegWrite(controller3_1_regwrite),
    .MemWrite(controller3_1_memwrite), .nPC_Sel(controller3_1_npc_sel), .ExtOp(controller3_1_extop),
    .ALUCtrl(controller3_1_aluctrl));
  Multiplexer #(.width(32)) multiplexer_2 (
    .in0(gpr1_1_rdata2), .in1(ext_1_out_3), .out(multiplexer_2_out), .sel(controller3_1_alusrc), .en(1'b1));
  ALU1 alu1_1 (
    .A(gpr1_1_rdata1), .B(multiplexer_2_out), .ALUCtr(controller3_1_aluctrl), .Result(alu1_1_result),
    .Zero(alu1_1_zero));
  DM dm_1 (
    .A(alu1_1_result[6:2]), .D(gpr1_1_rdata2), .MemToReg(controller3_1_memtoreg),
    .str(controller3_1_memwrite), .Clk(Clk_out), .Clr(Reset), .Result(alu1_1_result), .WData(dm_1_wdata));
  RAM #(.addrWidth(5), .dataWidth(32), .bus("separate")) ram_1 ();  // open: addr, din, data, str, sel, clk, ld, clr
  Multiplexer #(.width(32)) multiplexer_3 (.en(1'b1));  // open: in0, in1, out, sel

  // Notes on the sheet:
  //   16bits immidiate
  //   Func
  //   Shamt
  //   RD
  //   RT
  //   RS
  //   OP
  //   A
  //   WD
  //   there may be some mystery
endmodule

module ALU (
  input  [3:0] ALUCtr,
  input  [31:0] A,
  input  [31:0] B,
  input  [15:0] _16Bits,
  output [31:0] Result,
  output Zero
);

  wire or_2_out;
  wire [31:0] Adder_so, or_1_out, Subtractor_d;

  Adder32_main Adder (.A(A), .B(B), .Ci(1'b0), .So(Adder_so));  // open: Co
  Subber32 Subtractor (.Ci(1'b0), .A(A), .B(B), .D(Subtractor_d));  // open: Co
  assign or_1_out = A | B;  // OR_Gate or_1, 32 bits wide
  Multiplexer #(.select(4), .width(32)) multiplexer_1 (
    .in1(Adder_so), .in2(Subtractor_d), .in4(or_1_out), .in8({_16Bits, {16{1'b0}}}), .out(Result),
    .sel(ALUCtr));  // open: in0, in3, in5, in6, in7, in9, in10, in11, in12, in13, in14, in15, en
  or or_2 (or_2_out, Result[0], Result[1], Result[2], Result[3], Result[4], Result[5], Result[6], Result[7], Result[8], Result[9], Result[10], Result[11], Result[12], Result[13], Result[14], Result[15], Result[16], Result[17], Result[18], Result[19], Result[20], Result[21], Result[22], Result[23], Result[24], Result[25], Result[26], Result[27], Result[28], Result[29], Result[30], Result[31]);
  not not_1 (Zero, or_2_out);

  // Notes on the sheet:
  //   0-3:add
  //   3-5:subtract
  //   6-7:or
  //   there may be some problems
endmodule

module IFU (
  input  IfBeq,
  input  Zero,
  input  Clk,
  input  Reset,
  output [31:0] Instr
);

  wire and_1_out;
  wire [29:0] adder_1_out, multiplexer_1_out, register_1_q;

  // Probe on multiplexer_1_out
  // Probe on register_1_q
  and and_1 (and_1_out, IfBeq, Zero);
  Register #(.width(30)) register_1 (.D(adder_1_out), .en(1'b1), .Q(register_1_q), .clk(Clk), .clr(Reset));
  Multiplexer #(.width(30)) multiplexer_1 (
    .in0({30{1'b0}}), .in1({{14{1'b0}}, Instr[15:0]}), .out(multiplexer_1_out), .sel(and_1_out));  // open: en
  Adder #(.width(30)) adder_1 (.a(multiplexer_1_out), .b(register_1_q), .out(adder_1_out), .cin(1'b1));  // open: cout
  ROM #(.addrWidth(5), .dataWidth(32)) rom_1 (.addr(register_1_q[4:0]), .data(Instr));  // open: sel

  // Notes on the sheet:
  //   Sign_Ext?
  //   exists some mystery
  //   contents of rom_1 (hex, n*v repeats v):
  //   34210014 34420015 34630001 432021 3c040008 3c050009 a43021 833823 224021 1074823 ac260004 ac470003
  //   8c2a0000 8c2b0004 ac240000 8c65ffff 35ad0001 16d6021 1836023 116cfffe
  //   Can use Bit Extender
endmodule

// GPR
module GPR1 (
  input  [4:0] RS1,
  input  [4:0] RS2,
  input  RegWrite,
  input  [4:0] RD_WA,
  input  [31:0] WData,
  input  ResetReg,
  input  Clk,
  output [31:0] RData1,
  output [31:0] RData2
);

  wire decoder_1_out0, decoder_1_out1, decoder_1_out2, decoder_1_out3, decoder_1_out4, decoder_1_out5,
       decoder_1_out6, decoder_1_out7, decoder_1_out8, decoder_1_out9, decoder_1_out10, decoder_1_out11,
       decoder_1_out12, decoder_1_out13, decoder_1_out14, decoder_1_out15, decoder_1_out16, decoder_1_out17,
       decoder_1_out18, decoder_1_out19, decoder_1_out20, decoder_1_out21, decoder_1_out22, decoder_1_out23,
       decoder_1_out24, decoder_1_out25, decoder_1_out26, decoder_1_out27, decoder_1_out28, decoder_1_out29,
       decoder_1_out30, decoder_1_out31;
  wire [31:0] _0_q, _1_q, _2_q, _3_q, _4_q, _5_q, _6_q, _7_q, _8_q, _9_q, _10_q, _11_q, _12_q, _13_q, _14_q,
       _15_q, _16_q, _17_q, _18_q, _19_q, _20_q, _21_q, _22_q, _23_q, _24_q, _25_q, _26_q, _27_q, _28_q,
       _29_q, _30_q, _31_q;

  Decoder #(.select(5), .disabled(0)) decoder_1 (
    .out0(decoder_1_out0), .out1(decoder_1_out1), .out2(decoder_1_out2), .out3(decoder_1_out3),
    .out4(decoder_1_out4), .out5(decoder_1_out5), .out6(decoder_1_out6), .out7(decoder_1_out7),
    .out8(decoder_1_out8), .out9(decoder_1_out9), .out10(decoder_1_out10), .out11(decoder_1_out11),
    .out12(decoder_1_out12), .out13(decoder_1_out13), .out14(decoder_1_out14), .out15(decoder_1_out15),
    .out16(decoder_1_out16), .out17(decoder_1_out17), .out18(decoder_1_out18), .out19(decoder_1_out19),
    .out20(decoder_1_out20), .out21(decoder_1_out21), .out22(decoder_1_out22), .out23(decoder_1_out23),
    .out24(decoder_1_out24), .out25(decoder_1_out25), .out26(decoder_1_out26), .out27(decoder_1_out27),
    .out28(decoder_1_out28), .out29(decoder_1_out29), .out30(decoder_1_out30), .out31(decoder_1_out31),
    .sel(RD_WA), .en(RegWrite));
  Register #(.width(32)) _0 (.D(WData), .en(decoder_1_out0), .Q(_0_q), .clk(Clk), .clr(ResetReg));
  Register #(.width(32)) _4 (.D(WData), .en(decoder_1_out4), .Q(_4_q), .clk(Clk), .clr(ResetReg));
  Register #(.width(32)) _8 (.D(WData), .en(decoder_1_out8), .Q(_8_q), .clk(Clk), .clr(ResetReg));
  Register #(.width(32)) _12 (.D(WData), .en(decoder_1_out12), .Q(_12_q), .clk(Clk), .clr(ResetReg));
  Register #(.width(32)) _16 (.D(WData), .en(decoder_1_out16), .Q(_16_q), .clk(Clk), .clr(ResetReg));
  Register #(.width(32)) _20 (.D(WData), .en(decoder_1_out20), .Q(_20_q), .clk(Clk), .clr(ResetReg));
  Register #(.width(32)) _24 (.D(WData), .en(decoder_1_out24), .Q(_24_q), .clk(Clk), .clr(ResetReg));
  Register #(.width(32)) _28 (.D(WData), .en(decoder_1_out28), .Q(_28_q), .clk(Clk), .clr(ResetReg));
  Register #(.width(32)) _1 (.D(WData), .en(decoder_1_out1), .Q(_1_q), .clk(Clk), .clr(ResetReg));
  Register #(.width(32)) _5 (.D(WData), .en(decoder_1_out5), .Q(_5_q), .clk(Clk), .clr(ResetReg));
  Register #(.width(32)) _9 (.D(WData), .en(decoder_1_out9), .Q(_9_q), .clk(Clk), .clr(ResetReg));
  Register #(.width(32)) _13 (.D(WData), .en(decoder_1_out13), .Q(_13_q), .clk(Clk), .clr(ResetReg));
  Register #(.width(32)) _17 (.D(WData), .en(decoder_1_out17), .Q(_17_q), .clk(Clk), .clr(ResetReg));
  Register #(.width(32)) _21 (.D(WData), .en(decoder_1_out21), .Q(_21_q), .clk(Clk), .clr(ResetReg));
  Register #(.width(32)) _25 (.D(WData), .en(decoder_1_out25), .Q(_25_q), .clk(Clk), .clr(ResetReg));
  Register #(.width(32)) _29 (.D(WData), .en(decoder_1_out29), .Q(_29_q), .clk(Clk), .clr(ResetReg));
  Register #(.width(32)) _6 (.D(WData), .en(decoder_1_out6), .Q(_6_q), .clk(Clk), .clr(ResetReg));
  Register #(.width(32)) _2 (.D(WData), .en(decoder_1_out2), .Q(_2_q), .clk(Clk), .clr(ResetReg));
  Register #(.width(32)) _10 (.D(WData), .en(decoder_1_out10), .Q(_10_q), .clk(Clk), .clr(ResetReg));
  Register #(.width(32)) _14 (.D(WData), .en(decoder_1_out14), .Q(_14_q), .clk(Clk), .clr(ResetReg));
  Register #(.width(32)) _18 (.D(WData), .en(decoder_1_out18), .Q(_18_q), .clk(Clk), .clr(ResetReg));
  Register #(.width(32)) _22 (.D(WData), .en(decoder_1_out22), .Q(_22_q), .clk(Clk), .clr(ResetReg));
  Register #(.width(32)) _26 (.D(WData), .en(decoder_1_out26), .Q(_26_q), .clk(Clk), .clr(ResetReg));
  Register #(.width(32)) _30 (.D(WData), .en(decoder_1_out30), .Q(_30_q), .clk(Clk), .clr(ResetReg));
  Register #(.width(32)) _7 (.D(WData), .en(decoder_1_out7), .Q(_7_q), .clk(Clk), .clr(ResetReg));
  Register #(.width(32)) _3 (.D(WData), .en(decoder_1_out3), .Q(_3_q), .clk(Clk), .clr(ResetReg));
  Register #(.width(32)) _11 (.D(WData), .en(decoder_1_out11), .Q(_11_q), .clk(Clk), .clr(ResetReg));
  Register #(.width(32)) _15 (.D(WData), .en(decoder_1_out15), .Q(_15_q), .clk(Clk), .clr(ResetReg));
  Register #(.width(32)) _19 (.D(WData), .en(decoder_1_out19), .Q(_19_q), .clk(Clk), .clr(ResetReg));
  Register #(.width(32)) _23 (.D(WData), .en(decoder_1_out23), .Q(_23_q), .clk(Clk), .clr(ResetReg));
  Register #(.width(32)) _27 (.D(WData), .en(decoder_1_out27), .Q(_27_q), .clk(Clk), .clr(ResetReg));
  Register #(.width(32)) _31 (.D(WData), .en(decoder_1_out31), .Q(_31_q), .clk(Clk), .clr(ResetReg));
  Multiplexer #(.select(5), .width(32)) multiplexer_1 (
    .in0(_0_q), .in1(_1_q), .in2(_2_q), .in3(_3_q), .in4(_4_q), .in5(_5_q), .in6(_6_q), .in7(_7_q),
    .in8(_8_q), .in9(_9_q), .in10(_10_q), .in11(_11_q), .in12(_12_q), .in13(_13_q), .in14(_14_q),
    .in15(_15_q), .in16(_16_q), .in17(_17_q), .in18(_18_q), .in19(_19_q), .in20(_20_q), .in21(_21_q),
    .in22(_22_q), .in23(_23_q), .in24(_24_q), .in25(_25_q), .in26(_26_q), .in27(_27_q), .in28(_28_q),
    .in29(_29_q), .in30(_30_q), .in31(_31_q), .out(RData1), .sel(RS1));  // open: en
  Multiplexer #(.select(5), .width(32)) multiplexer_2 (
    .in0(_0_q), .in1(_1_q), .in2(_2_q), .in3(_3_q), .in4(_4_q), .in5(_5_q), .in6(_6_q), .in7(_7_q),
    .in8(_8_q), .in9(_9_q), .in10(_10_q), .in11(_11_q), .in12(_12_q), .in13(_13_q), .in14(_14_q),
    .in15(_15_q), .in16(_16_q), .in17(_17_q), .in18(_18_q), .in19(_19_q), .in20(_20_q), .in21(_21_q),
    .in22(_22_q), .in23(_23_q), .in24(_24_q), .in25(_25_q), .in26(_26_q), .in27(_27_q), .in28(_28_q),
    .in29(_29_q), .in30(_30_q), .in31(_31_q), .out(RData2), .sel(RS2));  // open: en
endmodule

// Control Unit
module Controller (
  input  [5:0] Op,
  input  [5:0] Func,
  output RegDst,
  output ALUSrc,
  output MemtoReg,
  output RegWrite,
  output MemWrite,
  output nPC_Sel,
  output ExtOp,
  output [2:0] ALUCtrl
);

  wire add_out, fcAdd_out, fcSub_out, lw_out, not_1_out, not_2_out, not_3_out, not_4_out, not_5_out,
       not_6_out, not_8_out, not_9_out, not_10_out, not_11_out, not_12_out, sub_out, sw_out;

  not not_1 (not_1_out, Op[5]);
  not not_2 (not_2_out, Op[4]);
  not not_3 (not_3_out, Op[3]);
  not not_4 (not_4_out, Op[2]);
  not not_5 (not_5_out, Op[1]);
  not not_6 (not_6_out, Op[0]);
  // NOT_Gate not_7 has open pins: in=Func[5], out=open
  not not_8 (not_8_out, Func[4]);
  not not_9 (not_9_out, Func[3]);
  and add (add_out, not_1_out, not_2_out, not_3_out, fcAdd_out, not_4_out, not_5_out, not_6_out);
  and sub (sub_out, not_1_out, not_2_out, not_3_out, fcSub_out, not_4_out, not_5_out, not_6_out);
  and ori (ALUCtrl[2], not_1_out, not_2_out, Op[3], Op[2], not_5_out, Op[0]);
  and lw (lw_out, Op[5], not_2_out, not_3_out, not_4_out, Op[1], Op[0]);
  and sw (sw_out, Op[5], not_2_out, Op[3], not_4_out, Op[1], Op[0]);
  and beq (nPC_Sel, not_1_out, not_2_out, not_3_out, Op[2], not_5_out, not_6_out);
  // AND_Gate lui has open pins: in0=not_6_out, in1=not_5_out, in2=not_4_out, in3=not_3_out, in4=Op[4], in5=Op[5], out=open
  not not_10 (not_10_out, Func[2]);
  or u_RegDst (RegDst, add_out, sub_out);
  not not_11 (not_11_out, Func[1]);
  or u_ALUSrc (ALUSrc, ALUCtrl[2], lw_out, sw_out);
  not not_12 (not_12_out, Func[0]);
  or u_RegWrite (RegWrite, add_out, sub_out, ALUCtrl[2], lw_out);
  buf u_MemtoReg (MemtoReg, lw_out);  // OR_Gate
  and fcAdd (fcAdd_out, Func[5], not_8_out, not_9_out, not_10_out, not_11_out, not_12_out);
  and fcSub (fcSub_out, Func[5], not_8_out, not_9_out, not_10_out, Func[1], not_12_out);
  buf u_MemWrite (MemWrite, sw_out);  // OR_Gate
  or u_ExtOp (ExtOp, lw_out, sw_out);
  or Add_2 (ALUCtrl[0], add_out, lw_out, sw_out);
  or Subtract (ALUCtrl[1], sub_out, nPC_Sel);

  // Notes on the sheet:
  //   nPC_Sel
  //   Or
endmodule

// CPU
module CPU0 (
  input  Reset
);

  wire alu_1_zero, Clk_out, controller2_1_alusrc, controller2_1_memtoreg, controller2_1_memwrite,
       controller2_1_npc_sel, controller2_1_regdst, controller2_1_regwrite;
  wire [3:0] controller2_1_aluctrl;
  wire [4:0] multiplexer_1_out;
  wire [15:0] ifu_1_instr;
  wire [31:0] alu_1_result, bit_extender_1_out, gpr1_1_rdata1, gpr1_1_rdata2, multiplexer_2_out,
       multiplexer_3_out, ram_1_data;
  wire [31:16] ifu_1_instr_2;

  Clock Clk (.out(Clk_out));
  IFU ifu_1 (
    .IfBeq(controller2_1_npc_sel), .Zero(alu_1_zero), .Clk(Clk_out), .Reset(Reset),
    .Instr({ifu_1_instr_2, ifu_1_instr}));
  Multiplexer #(.width(5)) multiplexer_1 (
    .in0(ifu_1_instr_2[20:16]), .in1(ifu_1_instr[15:11]), .out(multiplexer_1_out),
    .sel(controller2_1_regdst), .en(1'b1));
  assign bit_extender_1_out = {{16{1'b0}}, ifu_1_instr};  // Bit_Extender bit_extender_1
  GPR1 gpr1_1 (
    .RS1(ifu_1_instr_2[25:21]), .RS2(ifu_1_instr_2[20:16]), .RegWrite(controller2_1_regwrite),
    .RD_WA(multiplexer_1_out), .WData(multiplexer_3_out), .ResetReg(Reset), .Clk(Clk_out),
    .RData1(gpr1_1_rdata1), .RData2(gpr1_1_rdata2));
  Controller2 controller2_1 (
    .Op(ifu_1_instr_2[31:26]), .Func(ifu_1_instr[5:0]), .RegDst(controller2_1_regdst),
    .ALUSrc(controller2_1_alusrc), .MemtoReg(controller2_1_memtoreg), .RegWrite(controller2_1_regwrite),
    .MemWrite(controller2_1_memwrite), .nPC_Sel(controller2_1_npc_sel), .ALUCtrl(controller2_1_aluctrl));  // open: ExtOp
  Multiplexer #(.width(32)) multiplexer_2 (
    .in0(gpr1_1_rdata2), .in1(bit_extender_1_out), .out(multiplexer_2_out), .sel(controller2_1_alusrc),
    .en(1'b1));
  ALU alu_1 (
    .A(gpr1_1_rdata1), .B(multiplexer_2_out), ._16Bits(ifu_1_instr), .ALUCtr(controller2_1_aluctrl),
    .Result(alu_1_result), .Zero(alu_1_zero));
  RAM #(.addrWidth(5), .dataWidth(32), .bus("separate")) ram_1 (
    .addr(alu_1_result[6:2]), .din(gpr1_1_rdata2), .data(ram_1_data), .str(controller2_1_memwrite),
    .clk(Clk_out), .ld(1'b1), .clr(Reset));  // open: sel
  Multiplexer #(.width(32)) multiplexer_3 (
    .in0(alu_1_result), .in1(ram_1_data), .out(multiplexer_3_out), .sel(controller2_1_memtoreg), .en(1'b1));

  // Notes on the sheet:
  //   16bits immidiate
  //   Func
  //   Shamt
  //   RD
  //   RT
  //   RS
  //   OP
  //   A
  //   WD
  //   there may be some mystery
endmodule

// ControllerV2
module Controller1 (
  input  [5:0] Op,
  input  [5:0] Func,
  output RegDst,
  output ALUSrc,
  output MemtoReg,
  output RegWrite,
  output MemWrite,
  output nPC_Sel,
  output ExtOp,
  output [2:0] ALUCtrl
);

  wire Add_2_out, add_out, fcAdd_out, fcSub_out, lw_out, not_1_out, not_2_out, not_3_out, not_4_out,
       not_5_out, not_6_out, not_8_out, not_9_out, not_10_out, not_11_out, not_12_out, ori_out, sub_out,
       Subtract_out, sw_out;

  not not_1 (not_1_out, Op[5]);
  not not_2 (not_2_out, Op[4]);
  not not_3 (not_3_out, Op[3]);
  not not_4 (not_4_out, Op[1]);
  not not_5 (not_5_out, Op[2]);
  not not_6 (not_6_out, Op[0]);
  // NOT_Gate not_7 has open pins: in=Func[5], out=open
  not not_8 (not_8_out, Func[4]);
  not not_9 (not_9_out, Func[3]);
  and add (add_out, not_1_out, not_2_out, not_3_out, fcAdd_out, not_5_out, not_4_out, not_6_out);
  and sub (sub_out, not_1_out, not_2_out, not_3_out, fcSub_out, not_5_out, not_4_out, not_6_out);
  and ori (ori_out, not_1_out, not_2_out, Op[3], Op[2], not_4_out, Op[0]);
  and lw (lw_out, Op[5], not_2_out, not_3_out, not_5_out, Op[1], Op[0]);
  and sw (sw_out, Op[5], not_2_out, Op[3], not_5_out, Op[1], Op[0]);
  and beq (nPC_Sel, not_1_out, not_2_out, not_3_out, Op[2], not_4_out, not_6_out);
  not not_10 (not_10_out, Func[2]);
  or u_RegDst (RegDst, add_out, sub_out);
  not not_11 (not_11_out, Func[1]);
  or u_ALUSrc (ALUSrc, ori_out, lw_out, sw_out);
  not not_12 (not_12_out, Func[0]);
  or u_RegWrite (RegWrite, add_out, sub_out, ori_out, lw_out);
  buf u_MemtoReg (MemtoReg, lw_out);  // OR_Gate
  and fcAdd (fcAdd_out, Func[5], not_8_out, not_9_out, not_10_out, not_11_out, not_12_out);
  and fcSub (fcSub_out, Func[5], not_8_out, not_9_out, not_10_out, Func[1], not_12_out);
  buf u_MemWrite (MemWrite, sw_out);  // OR_Gate
  or u_ExtOp (ExtOp, lw_out, sw_out);
  or Add_2 (Add_2_out, add_out, lw_out, sw_out);
  or Subtract (Subtract_out, sub_out, nPC_Sel);

  assign ALUCtrl = Func[2:0];

  // Other names for the same wires on the sheet: _1[2:0] = Func[2:0]

  // Notes on the sheet:
  //   nPC_Sel
  //   Or
endmodule

// ControllerV3
module Controller2 (
  input  [5:0] Op,
  input  [5:0] Func,
  output RegDst,
  output ALUSrc,
  output MemtoReg,
  output RegWrite,
  output MemWrite,
  output nPC_Sel,
  output ExtOp,
  output [3:0] ALUCtrl
);

  wire add_out, fcAdd_out, fcSub_out, not_1_out, not_2_out, not_3_out, not_4_out, not_5_out, not_6_out,
       not_8_out, not_9_out, not_10_out, not_11_out, sub_out;

  not not_1 (not_1_out, Op[5]);
  not not_2 (not_2_out, Op[4]);
  not not_3 (not_3_out, Op[3]);
  not not_4 (not_4_out, Op[1]);
  not not_5 (not_5_out, Op[2]);
  not not_6 (not_6_out, Op[0]);
  // NOT_Gate not_7 has open pins: in=Func[5], out=open
  not not_8 (not_8_out, Func[3]);
  not not_9 (not_9_out, Func[4]);
  and add (add_out, not_1_out, not_2_out, not_3_out, fcAdd_out, not_5_out, not_4_out, not_6_out);
  and sub (sub_out, not_1_out, not_2_out, not_3_out, fcSub_out, not_5_out, not_4_out, not_6_out);
  and ori (ALUCtrl[2], not_1_out, not_2_out, Op[3], Op[2], not_4_out, Op[0]);
  and lw (MemtoReg, Op[5], not_2_out, not_3_out, not_5_out, Op[1], Op[0]);
  and sw (MemWrite, Op[5], not_2_out, Op[3], not_5_out, Op[1], Op[0]);
  and beq (nPC_Sel, not_1_out, not_2_out, not_3_out, Op[2], not_4_out, not_6_out);
  and lui (ALUCtrl[3], Op[0], Op[1], Op[2], Op[3], not_2_out, not_1_out);
  not not_10 (not_10_out, Func[2]);
  or u_RegDst (RegDst, add_out, sub_out);
  not not_11 (not_11_out, Func[1]);
  or u_ALUSrc (ALUSrc, ALUCtrl[2], MemtoReg, MemWrite);
  // NOT_Gate not_12 has open pins: in=Func[0], out=open
  or u_RegWrite (RegWrite, add_out, sub_out, ALUCtrl[3], ALUCtrl[2], MemtoReg);
  and fcAdd (fcAdd_out, Func[5], not_9_out, not_8_out, not_10_out, not_11_out, Func[0]);
  and fcSub (fcSub_out, Func[5], not_9_out, not_8_out, not_10_out, Func[1], Func[0]);
  or u_ExtOp (ExtOp, MemtoReg, ALUCtrl[3], MemWrite);
  or Add_2 (ALUCtrl[0], add_out, MemtoReg, MemWrite);
  or Subtract (ALUCtrl[1], sub_out, nPC_Sel);

  // Other names for the same wires on the sheet: _1[2:0] = Func[2:0]

  // Notes on the sheet:
  //   MemToReg
  //   MemWrite
  //   nPC_Sel
  //   Or
endmodule

module EXT (
  input  ExtOP,
  input  [15:0] _16Bits,
  output [31:0] out_3
);

  wire [31:0] bit_extender_1_out;

  assign bit_extender_1_out = {{16{1'b0}}, _16Bits};  // Bit_Extender bit_extender_1
  Multiplexer #(.width(32)) multiplexer_1 (
    .in0(bit_extender_1_out), .in1({_16Bits, {16{1'b0}}}), .out(out_3), .sel(ExtOP));  // open: en
endmodule

// ControllerV4
module Controller3 (
  input  [5:0] Op,
  input  [5:0] Func,
  output RegDst,
  output ALUSrc,
  output MemtoReg,
  output RegWrite,
  output MemWrite,
  output nPC_Sel,
  output ExtOp,
  output [3:0] ALUCtrl
);

  wire add_out, fcAdd_out, fcSub_out, not_1_out, not_2_out, not_3_out, not_4_out, not_5_out, not_6_out,
       not_8_out, not_9_out, not_10_out, not_11_out, sub_out;

  not not_1 (not_1_out, Op[5]);
  not not_2 (not_2_out, Op[4]);
  not not_3 (not_3_out, Op[3]);
  not not_4 (not_4_out, Op[2]);
  not not_5 (not_5_out, Op[1]);
  not not_6 (not_6_out, Op[0]);
  // NOT_Gate not_7 has open pins: in=Func[5], out=open
  not not_8 (not_8_out, Func[3]);
  not not_9 (not_9_out, Func[4]);
  and add (add_out, not_1_out, not_2_out, not_3_out, fcAdd_out, not_4_out, not_5_out, not_6_out);
  and sub (sub_out, not_1_out, not_2_out, not_3_out, fcSub_out, not_4_out, not_5_out, not_6_out);
  and ori (ALUCtrl[2], not_1_out, not_2_out, Op[3], Op[2], not_5_out, Op[0]);
  and lw (MemtoReg, Op[5], not_2_out, not_3_out, not_4_out, Op[1], Op[0]);
  and sw (MemWrite, Op[5], not_2_out, Op[3], not_4_out, Op[1], Op[0]);
  and beq (nPC_Sel, not_1_out, not_2_out, not_3_out, Op[2], not_5_out, not_6_out);
  and lui (ALUCtrl[3], Op[0], Op[1], Op[2], Op[3], not_2_out, not_1_out);
  not not_10 (not_10_out, Func[2]);
  or u_RegDst (RegDst, add_out, sub_out);
  not not_11 (not_11_out, Func[1]);
  or u_ALUSrc (ALUSrc, ALUCtrl[2], MemtoReg, ALUCtrl[3], MemWrite);
  // NOT_Gate not_12 has open pins: in=Func[0], out=open
  or u_RegWrite (RegWrite, add_out, sub_out, ALUCtrl[3], ALUCtrl[2], MemtoReg);
  and fcAdd (fcAdd_out, Func[5], not_9_out, not_8_out, not_10_out, not_11_out, Func[0]);
  and fcSub (fcSub_out, Func[5], not_9_out, not_8_out, not_10_out, Func[1], Func[0]);
  or Add_2 (ALUCtrl[0], add_out, MemtoReg, MemWrite);
  or Subtract (ALUCtrl[1], sub_out, nPC_Sel);

  assign ExtOp = ALUCtrl[3];

  // Other names for the same wires on the sheet: _1[2:0] = Func[2:0]

  // Notes on the sheet:
  //   MemToReg
  //   MemWrite
  //   nPC_Sel
  //   ExtOp
  //   Or
endmodule

// ALUV2
module ALU1 (
  input  [3:0] ALUCtr,
  input  [31:0] A,
  input  [31:0] B,
  output [31:0] Result,
  output Zero
);

  wire or_2_out;
  wire [31:0] Adder_so, or_1_out, Subtractor_d;

  Adder32_main Adder (.A(A), .B(B), .Ci(1'b0), .So(Adder_so));  // open: Co
  Subber32 Subtractor (.Ci(1'b0), .A(A), .B(B), .D(Subtractor_d));  // open: Co
  assign or_1_out = A | B;  // OR_Gate or_1, 32 bits wide
  Multiplexer #(.select(4), .width(32)) multiplexer_1 (
    .in1(Adder_so), .in2(Subtractor_d), .in4(or_1_out), .in8(B), .out(Result), .sel(ALUCtr));  // open: in0, in3, in5, in6, in7, in9, in10, in11, in12, in13, in14, in15, en
  or or_2 (or_2_out, Result[0], Result[1], Result[2], Result[3], Result[4], Result[5], Result[6], Result[7], Result[8], Result[9], Result[10], Result[11], Result[12], Result[13], Result[14], Result[15], Result[16], Result[17], Result[18], Result[19], Result[20], Result[21], Result[22], Result[23], Result[24], Result[25], Result[26], Result[27], Result[28], Result[29], Result[30], Result[31]);
  not not_1 (Zero, or_2_out);

  // Notes on the sheet:
  //   0-3:add
  //   3-5:subtract
  //   6-7:or
  //   there may be some problems
endmodule

// DataMemory
module DM (
  input  [4:0] A,
  input  [31:0] D,
  input  MemToReg,
  input  str,
  input  Clk,
  input  Clr,
  input  [31:0] Result,
  output [31:0] WData
);

  wire [31:0] ram_1_data;

  RAM #(.addrWidth(5), .dataWidth(32), .bus("separate")) ram_1 (
    .addr(A), .din(D), .data(ram_1_data), .str(str), .clk(Clk), .ld(1'b1), .clr(Clr));  // open: sel
  Multiplexer #(.width(32)) multiplexer_1 (.in0(Result), .in1(ram_1_data), .out(WData), .sel(MemToReg), .en(1'b1));
  Multiplexer #(.select(3)) multiplexer_2 ();  // open: in0, in1, in2, in3, in4, in5, in6, in7, out, sel, en
endmodule
